# Fritzing sketch switch (saved by Fritzing 0.9.6b)
breadboards: 1

parts:
  S1 = SWITCH-MOMENTARY-2 [package=tactile-pth-12mm]
  Part1 = Arduino Nano (Rev3.0) (ICSP)
  S2 = Pushbutton [package="[THT]"]
  S3 = Pushbutton [package="[THT]"]
  VCC2 = 4 x AAA Battery Mount
  M1 = DC Motor
  MCU1 = Raspberry Pi Zero
  D1 = SOLAR-IXYS [package=solarbit-12x1]  # not connected

nets:
  N1: S1.2, Part1.GND, VCC2.-, MCU1.pin_2, MCU1.pin_4
  N2: Part1.D10, S2.Pin_3, S2.Pin_4, M1.pin_2
  N3: Part1.VIN, Part1.AREF, S2.Pin_1, S2.Pin_2, S3.Pin_3, S3.Pin_4, VCC2.+
  N4: Part1.D13/SCK, S3.Pin_1, S3.Pin_2, M1.pin_1

notes:
  Enviro+ shield + PMS5003 sensor
  18650x4 shield
